# Fritzing sketch Schematic (saved by Fritzing 0.9.3b)
breadboards: 1

parts:
  Raspberry_Pi_1 = Raspberry Pi 3 [part_number=RPI-3-V1.2]
  M1 = MakerFocus MAX30102
  DS2 = DS18B20 1-Wire Temperature Sensor [part_number=DS18B20]
  R1 = Resistor [tolerance=±5% resistance=4.7k package="0402 [SMD]"]
  LCM1602_IIC1 = LCM1602 IIC [part_number="LCM1602 IIC" chip_label="LCM1602 IIC" package="DIP (Dual Inline) [THT]"]
  LCD1 = LCD screen
  LED3 = LED - 5mm [color="Blue (430nm)" package="5 mm [THT]"]
  LED4 = LED - 5mm [color="Green (570nm)" package="5 mm [THT]"]
  R3 = Resistor [tolerance=±5% resistance=220 package="0402 [SMD]"]
  R4 = Resistor [tolerance=±5% resistance=220 package="0402 [SMD]"]
  LED5 = LED - 5mm [color="Red (633nm)" package="5 mm [THT]"]
  R5 = Resistor [tolerance=±5% resistance=220 package="0402 [SMD]"]

nets:
  3V3: Raspberry_Pi_1.3v3, Raspberry_Pi_1.3V3, M1.VIN, DS2.VDD, R1.Pin_0
  N1: Raspberry_Pi_1.GPIO2, M1.SDA, LCM1602_IIC1.SDA
  N2: Raspberry_Pi_1.GPIO3, M1.SCL, LCM1602_IIC1.SCL
  N3: Raspberry_Pi_1.GPIO4, M1.INT
  N4: Raspberry_Pi_1.GPIO17, DS2.DQ, R1.Pin_1
  N5: Raspberry_Pi_1.GPIO21, LED5.anode
  GND: Raspberry_Pi_1.GND, M1.GND, DS2.GND, LCM1602_IIC1.GND, LED3.cathode, LED4.cathode, R3.Pin_0, R3.Pin_1, R4.Pin_0, R4.Pin_1, LED5.cathode, R5.Pin_0, R5.Pin_1
  N6: Raspberry_Pi_1.GPIO8, LED3.anode
  N7: Raspberry_Pi_1.GPIO25, LED4.anode
  5V: Raspberry_Pi_1.5V, LCM1602_IIC1.VCC
  VSS: LCM1602_IIC1.VSS, LCD1.VSS
  VDD: LCM1602_IIC1.VDD, LCD1.VDD
  N8: LCM1602_IIC1.V0, LCD1.V0
  N9: LCM1602_IIC1.RS, LCD1.RS
  N10: LCM1602_IIC1.RW, LCD1.R/W
  N11: LCM1602_IIC1.E, LCD1.E
  N12: LCM1602_IIC1.D0, LCD1.DB0
  N13: LCM1602_IIC1.D1, LCD1.DB1
  N14: LCM1602_IIC1.D2, LCD1.DB2
  N15: LCM1602_IIC1.D3, LCD1.DB3
  N16: LCM1602_IIC1.D4, LCD1.DB4
  N17: LCM1602_IIC1.D5, LCD1.DB5
  N18: LCM1602_IIC1.D6, LCD1.DB6
  N19: LCM1602_IIC1.D7, LCD1.DB7
  N20: LCM1602_IIC1.A, LCD1.LED+
  N21: LCM1602_IIC1.K, LCD1.LED-
  N22: LCM1602_IIC1.LED_A, LCM1602_IIC1.LED_B

custom parts:
  MakerFocus MAX30102: Oximeter module using the MAX30102 chip. As usual, if you want the mounting holes in pcb, you need to drag a hole over the pad in silkscreen to actually drill the hole (by default they are not drilled)
  LCM1602 IIC: I2C-Module to use a 1602 or 2004 LCD on with the wire.h libory Serial LCD Modul
